# Fritzing sketch schematics (saved by Fritzing 0.9.3b)

parts:
  Part1 = Arduino Uno (Rev3)
  LED1 = LEDs [package=led10mm]
  MIC1 = MAX4466 Electret Microphone Breakout Board
  KY-2 = Keyes Relay [package=THT]

nets:
  N1: Part1.A0, MIC1.out
  N2: Part1.D8, KY-2.ground
  N3: Part1.D9_PWM, LED1.A
  GND: Part1.GND, LED1.C, MIC1.GND, KY-2.power
  3V3: Part1.3V3, MIC1.VCC
  N4: Part1.5V, KY-2.signal

notes:
  Connected to power supply
  Order of pins on your relay module might differ
  LED for lighting up the Christmas star
  Mic for detecting claps
  Power cord continues to lights
  Power cord socket
  - connected to power supply

custom parts:
  MAX4466 Electret Microphone Breakout Board: MAX4466 Electrec Microphone Breakout Board
  Keyes Relay: The Keyes 5V relay module is suitable for SCM development, home appliance control. It uses a 5V~12V TIL control signal which can control DC / AC signal.
